// Logisim project project2.circ as structural Verilog: 8 circuits, main circuit main
module main (
);

  wire bcontrol_enbranch, clock_1_out, control_1_alusrc, control_1_enablewrite, control_1_extendselect,
       control_1_hilowrite, control_1_ld, control_1_memormd, control_1_opselect, control_1_str,
       fields_1_subop, Halt, JALSelect, jcontrol_jselect, LEDControl, LISelect, not_1_out;
  wire [1:0] control_1_aluop;
  wire [2:0] fields_1_rs;
  wire [3:0] BranchOp, multiplexer_2_out, multiplexer_2_out_2, undriven_2;
  wire [7:0] adder_1_out, bit_extender_4_out, BrAddress, multiplexer_1_out, multiplexer_7_out, register_1_q,
       undriven;
  wire [15:0] alu_1_output, bit_extender_1_out, bit_extender_2_out, bit_extender_3_out, HexLED,
       mult_div_1_output, multiplexer_3_out, multiplexer_4_out, multiplexer_5_out, multiplexer_6_out,
       multiplexer_8_out, ram_1_data, regmem_1_read_data_2, rom_1_data;
  wire [15:8] multiplexer_2_out_3;

  Hex_Digit_Display hex_digit_display_1 (.value(multiplexer_2_out_3[15:12]));  // open: dp
  Multiplexer #(.width(8), .enable("false")) multiplexer_1 (
    .in0(multiplexer_7_out), .in1(undriven), .out(multiplexer_1_out), .sel(jcontrol_jselect));
  Register register_1 (.D(multiplexer_1_out), .en(1'b1), .Q(register_1_q), .clk(clock_1_out));  // open: clr
  Clock clock_1 (.out(clock_1_out));
  Hex_Digit_Display hex_digit_display_2 (.value(multiplexer_2_out_2));  // open: dp
  Hex_Digit_Display hex_digit_display_3 (.value(multiplexer_2_out_3[11:8]));  // open: dp
  Hex_Digit_Display hex_digit_display_4 (.value(multiplexer_2_out));  // open: dp
  Multiplexer #(.width(16), .enable("false")) multiplexer_2 (
    .in1(HexLED), .out({multiplexer_2_out_3, multiplexer_2_out_2, multiplexer_2_out}), .sel(LEDControl));  // open: in0
  ROM #(.dataWidth(16)) rom_1 (.addr(register_1_q), .data(rom_1_data), .sel(1'b1));
  LED u_halt (.in(Halt));
  assign bit_extender_1_out = {{8{1'b0}}, adder_1_out};  // Bit_Extender bit_extender_1
  Adder adder_1 (.a(register_1_q), .b(8'h1), .out(adder_1_out));  // open: cin, cout
  FIELDS fields_1 (
    .Instruction(rom_1_data), .Opcode(BranchOp), .RS(fields_1_rs), .Immediate(BrAddress),
    .Subop(fields_1_subop));
  JCONTROL jcontrol (
    .RS(HexLED), .Immediate(BrAddress), .Opcode(BranchOp), .Output(undriven), .JSelect(jcontrol_jselect),
    .JALSelect(JALSelect));
  Multiplexer #(.width(16), .enable("false")) multiplexer_3 (
    .in0(multiplexer_8_out), .in1(bit_extender_1_out), .out(multiplexer_3_out), .sel(JALSelect));
  REGMEM regmem_1 (
    .EnableWrite(control_1_enablewrite), .Read_Register_1(fields_1_rs), .Read_Register_2(BrAddress[7:5]),
    .RegWrite(fields_1_rs), .WriteData(multiplexer_4_out), .Read_Data_1(HexLED),
    .Read_Data_2(regmem_1_read_data_2), .Clock(clock_1_out));
  Multiplexer #(.width(16), .enable("false")) multiplexer_4 (
    .in0(multiplexer_3_out), .in1(bit_extender_2_out), .out(multiplexer_4_out), .sel(LISelect));
  CONTROL control_1 (
    .opcode3(BranchOp[0]), .opcode2(BranchOp[1]), .opcode1(BranchOp[2]), .opcode0(BranchOp[3]),
    .subop(fields_1_subop), .HaltControl(Halt), .LEDControl(LEDControl), .LISelect(LISelect),
    .OPselect(control_1_opselect), .HiLoWrite(control_1_hilowrite), .MEMorMD(control_1_memormd),
    .str(control_1_str), .ld(control_1_ld), .ExtendSelect(control_1_extendselect), .ALUop(control_1_aluop),
    .ALUsrc(control_1_alusrc), .EnableWrite(control_1_enablewrite));
  assign bit_extender_2_out = {{8{BrAddress[7]}}, BrAddress};  // Bit_Extender bit_extender_2
  assign bit_extender_3_out = {{8{1'b0}}, BrAddress};  // Bit_Extender bit_extender_3
  Multiplexer #(.width(16), .enable("false")) multiplexer_5 (
    .in0(regmem_1_read_data_2), .in1(multiplexer_6_out), .out(multiplexer_5_out), .sel(control_1_alusrc));
  Multiplexer #(.width(16), .enable("false")) multiplexer_6 (
    .in0(bit_extender_2_out), .in1(bit_extender_3_out), .out(multiplexer_6_out), .sel(control_1_extendselect));
  BCONTROL bcontrol (.Opcode(BranchOp), .CompVals(undriven_2), .EnBranch(bcontrol_enbranch));
  ALU alu_1 (
    .A(HexLED), .B(multiplexer_5_out), .Operation(control_1_aluop), .CompVals(undriven_2),
    .Output(alu_1_output));
  MULT_DIV mult_div_1 (
    .RS(HexLED), .RT(regmem_1_read_data_2), .Clock(clock_1_out), .OPselect(control_1_opselect),
    .HiLoWrite(control_1_hilowrite), .Output(mult_div_1_output));
  Multiplexer #(.width(8), .enable("false")) multiplexer_7 (
    .in0(adder_1_out), .in1(BrAddress), .out(multiplexer_7_out), .sel(bcontrol_enbranch));
  Bit_Extender #(.in_width(16), .out_width(8)) bit_extender_4 (.in(alu_1_output), .out(bit_extender_4_out));
  not not_1 (not_1_out, clock_1_out);
  RAM #(.dataWidth(16), .bus("separate")) ram_1 (
    .addr(bit_extender_4_out), .din(regmem_1_read_data_2), .data(ram_1_data), .str(control_1_str),
    .sel(1'b1), .clk(not_1_out), .ld(control_1_ld));  // open: clr
  Multiplexer #(.width(16), .enable("false")) multiplexer_8 (
    .in0(ram_1_data), .in1(mult_div_1_output), .out(multiplexer_8_out), .sel(control_1_memormd));

  // Notes on the sheet:
  //   PC
  //   Instruction Memory
  //   contents of rom_1 (hex, n*v repeats v):
  //   100a f20c 80
  //   PC = PC + 1
  //   CONTROL
  //   ALUsrc
  //   ExtendSelect
  //   OPselect
  //   HiLoWrite
  //   Data Memory
  //   have 2nd output for branch control
  //   to control whether instruction meets
  //   corresponding branch condition
  //   MEMorMD
  //   0 for mem ops, 1 for HI/LO
endmodule

module REGMEM (
  input  EnableWrite,
  input  [2:0] Read_Register_1,
  input  [2:0] Read_Register_2,
  input  [2:0] RegWrite,
  input  [15:0] WriteData,
  input  Clock,
  output [15:0] Read_Data_1,
  output [15:0] Read_Data_2
);

  wire and_1_out;
  wire [15:0] demultiplexer_1_out0, demultiplexer_1_out1, demultiplexer_1_out2, demultiplexer_1_out3,
       demultiplexer_1_out4, demultiplexer_1_out5, demultiplexer_1_out6, demultiplexer_1_out7, r0_q, r1_q,
       r2_q, r3_q, r4_q, r5_q, r6_q, r7_q;

  Demultiplexer #(.select(3), .width(16), .enable("false")) demultiplexer_1 (
    .out0(demultiplexer_1_out0), .out1(demultiplexer_1_out1), .out2(demultiplexer_1_out2),
    .out3(demultiplexer_1_out3), .out4(demultiplexer_1_out4), .out5(demultiplexer_1_out5),
    .out6(demultiplexer_1_out6), .out7(demultiplexer_1_out7), .in(WriteData), .sel(RegWrite));
  and and_1 (and_1_out, EnableWrite, Clock);
  Register #(.width(16)) r0 (.D(demultiplexer_1_out0), .Q(r0_q), .clk(and_1_out));  // open: en, clr
  Register #(.width(16)) r1 (.D(demultiplexer_1_out1), .Q(r1_q), .clk(and_1_out));  // open: en, clr
  Register #(.width(16)) r2 (.D(demultiplexer_1_out2), .Q(r2_q), .clk(and_1_out));  // open: en, clr
  Register #(.width(16)) r3 (.D(demultiplexer_1_out3), .Q(r3_q), .clk(and_1_out));  // open: en, clr
  Register #(.width(16)) r4 (.D(demultiplexer_1_out4), .Q(r4_q), .clk(and_1_out));  // open: en, clr
  Register #(.width(16)) r5 (.D(demultiplexer_1_out5), .Q(r5_q), .clk(and_1_out));  // open: en, clr
  Register #(.width(16)) r6 (.D(demultiplexer_1_out6), .Q(r6_q), .clk(and_1_out));  // open: en, clr
  Register #(.width(16)) r7 (.D(demultiplexer_1_out7), .Q(r7_q), .clk(and_1_out));  // open: en, clr
  Multiplexer #(.select(3), .width(16), .enable("false")) multiplexer_1 (
    .in0(r0_q), .in1(r1_q), .in2(r2_q), .in3(r3_q), .in4(r4_q), .in5(r5_q), .in6(r6_q), .in7(r7_q),
    .out(Read_Data_1), .sel(Read_Register_1));
  Multiplexer #(.select(3), .width(16), .enable("false")) multiplexer_2 (
    .in0(r0_q), .in1(r1_q), .in2(r2_q), .in3(r3_q), .in4(r4_q), .in5(r5_q), .in6(r6_q), .in7(r7_q),
    .out(Read_Data_2), .sel(Read_Register_2));

  // Other names for the same wires on the sheet: ReadReg1[2:0] = Read_Register_1; ReadReg2[2:0] = Read_Register_2
endmodule

module ALU (
  input  [3:0] CompVals,
  input  [15:0] A,
  input  [15:0] B,
  input  [1:0] Operation,
  output [15:0] Output
);

  wire [15:0] adder_1_out, and_1_out, nor_1_out, subtractor_1_out;

  Adder #(.width(16)) adder_1 (.a(A), .b(B), .out(adder_1_out), .cin(1'b0));  // open: cout
  Subtractor #(.width(16)) subtractor_1 (.a(A), .b(B), .out(subtractor_1_out), .bin(1'b0));  // open: bout
  assign and_1_out = A & B;  // AND_Gate and_1, 16 bits wide
  assign nor_1_out = ~(A | B);  // NOR_Gate nor_1, 16 bits wide
  Multiplexer #(.select(2), .width(16), .enable("false")) multiplexer_1 (
    .in0(adder_1_out), .in1(subtractor_1_out), .in2(nor_1_out), .in3(and_1_out), .out(Output), .sel(Operation));
  Subtractor #(.width(16)) subtractor_2 (.a({16{1'b0}}), .b(A), .bout(CompVals[1]));  // open: out, bin
  or or_1 (CompVals[2], A[0], A[1], A[2], A[3], A[4], A[5], A[6], A[7], A[8], A[9], A[10], A[11], A[12], A[13], A[14], A[15]);
  not not_1 (CompVals[0], CompVals[1]);
  not not_2 (CompVals[3], CompVals[2]);

  // Other names for the same wires on the sheet: Branch_Comps[15:0] = A

  // Notes on the sheet:
  //   For conditional branching, each condition is represented
  //   by and individual bit within a 4-bit value that is passed into
  //   the branch control unit
  //   bn
  //   bp
  //   bx
  //   bz
  //   Branch Conditions: bp == 0101
  //   bn == 0110
  //   bx == 0101 || 0110
  //   bz == 1001 || 1010
endmodule

module FIELDS (
  input  [15:0] Instruction,
  output [3:0] Opcode,
  output [2:0] RS,
  output [7:0] Immediate,
  output Subop
);


  assign Immediate = Instruction[8:1];
  assign Opcode = Instruction[15:12];
  assign RS = Instruction[11:9];
  assign Subop = Instruction[0];
endmodule

// M/D
module MULT_DIV (
  input  OPselect,
  input  [15:0] RS,
  input  HiLoWrite,
  input  [15:0] RT,
  input  Clock,
  output [15:0] Output
);

  wire [15:0] divider_1_out, divider_1_rem, LO_q, multiplexer_1_out, multiplexer_2_out, multiplier_1_cout,
       multiplier_1_out, register_1_q;

  Divider #(.width(16)) divider_1 (.a(RS), .b(RT), .out(divider_1_out), .rem(divider_1_rem));  // open: upper
  Multiplier #(.width(16)) multiplier_1 (
    .a(RS), .b(RT), .out(multiplier_1_out), .cout(multiplier_1_cout));  // open: cin
  Multiplexer #(.width(16), .enable("false")) multiplexer_1 (
    .in0(divider_1_out), .in1(multiplier_1_out), .out(multiplexer_1_out), .sel(OPselect));
  Multiplexer #(.width(16), .enable("false")) multiplexer_2 (
    .in0(divider_1_rem), .in1(multiplier_1_cout), .out(multiplexer_2_out), .sel(OPselect));
  Register #(.width(16)) LO (.D(multiplexer_1_out), .en(HiLoWrite), .Q(LO_q), .clk(Clock));  // open: clr
  Register #(.width(16)) register_1 (
    .D(multiplexer_2_out), .en(HiLoWrite), .Q(register_1_q), .clk(Clock));  // open: clr
  Multiplexer #(.width(16), .enable("false")) multiplexer_3 (
    .in0(LO_q), .in1(register_1_q), .out(Output), .sel(OPselect));

  // Notes on the sheet:
  //   Multiplication & Division Substructure
  //   OPselect: 0 for div || mlo, 1 for mult || mhi
  //   HiLoWrite: 0 for output, 1 for input
endmodule

module CONTROL (
  input  opcode3,
  input  opcode2,
  input  opcode1,
  input  opcode0,
  input  subop,
  output HaltControl,
  output LEDControl,
  output LISelect,
  output OPselect,
  output HiLoWrite,
  output MEMorMD,
  output str,
  output ld,
  output ExtendSelect,
  output [1:0] ALUop,
  output ALUsrc,
  output EnableWrite
);

  wire and_8_out, and_9_out, and_10_out, and_11_out, and_12_out, and_13_out, and_14_out, not_1_out,
       not_2_out, not_3_out, not_5_out, not_6_out, not_7_out, not_8_out, not_9_out, not_10_out, not_11_out,
       not_12_out, not_13_out, not_14_out, not_15_out, not_16_out, not_17_out, not_18_out, not_19_out,
       not_20_out, not_21_out, not_22_out, not_23_out, not_24_out, not_25_out, not_26_out, not_27_out;

  not not_1 (not_1_out, opcode2);
  not not_2 (not_2_out, opcode2);
  not not_3 (not_3_out, opcode0);
  and and_1 (LISelect, opcode3, opcode1);
  not not_4 (HiLoWrite, opcode2);
  not not_5 (not_5_out, opcode3);
  not not_6 (not_6_out, opcode1);
  not not_7 (not_7_out, opcode0);
  not not_8 (not_8_out, opcode1);
  not not_9 (not_9_out, opcode0);
  not not_10 (not_10_out, subop);
  not not_11 (not_11_out, opcode2);
  not not_12 (not_12_out, opcode2);
  not not_13 (not_13_out, opcode1);
  not not_14 (not_14_out, opcode0);
  not not_15 (not_15_out, subop);
  not not_16 (not_16_out, opcode3);
  not not_17 (not_17_out, opcode2);
  not not_18 (not_18_out, opcode1);
  not not_19 (not_19_out, opcode3);
  not not_20 (not_20_out, opcode2);
  not not_21 (not_21_out, opcode0);
  not not_22 (not_22_out, opcode3);
  not not_23 (not_23_out, opcode1);
  not not_24 (not_24_out, opcode0);
  not not_25 (not_25_out, opcode1);
  not not_26 (not_26_out, opcode0);
  not not_27 (not_27_out, subop);
  and and_2 (HaltControl, opcode3, not_1_out, opcode1, opcode0);
  and and_3 (LEDControl, opcode3, not_2_out, opcode1, not_3_out);
  and and_4 (MEMorMD, not_5_out, opcode2);
  and and_5 (str, opcode3, opcode2, not_6_out, not_7_out, subop);
  and and_6 (ld, opcode3, opcode2, not_8_out, not_9_out, not_10_out);
  and and_7 (ExtendSelect, not_11_out, subop);
  and and_8 (and_8_out, not_12_out, not_13_out, not_14_out, subop);
  and and_9 (and_9_out, opcode1, not_15_out);
  and and_10 (and_10_out, not_16_out, not_17_out, not_18_out);
  and and_11 (and_11_out, not_19_out, not_20_out, not_21_out);
  and and_12 (and_12_out, not_22_out, not_23_out, not_24_out);
  and and_13 (and_13_out, opcode2, not_25_out, not_26_out, not_27_out);
  and and_14 (and_14_out, opcode3, opcode2, opcode1, opcode0);
  or or_1 (ALUop[0], and_8_out, and_9_out);
  or or_2 (EnableWrite, and_10_out, and_11_out, and_12_out, and_13_out, and_14_out);

  assign ALUop[1] = opcode1;
  assign ALUsrc = opcode0;
  assign OPselect = subop;
endmodule

module BCONTROL (
  input  [3:0] Opcode,
  input  [3:0] CompVals,
  output EnBranch
);

  wire and_1_out, and_2_out, and_3_out, and_4_out, and_5_out, and_6_out, and_7_out, and_8_out, not_1_out,
       not_2_out, not_3_out, not_4_out, not_5_out, not_6_out, not_7_out, not_8_out;

  not not_1 (not_1_out, Opcode[1]);
  not not_2 (not_2_out, Opcode[3]);
  not not_3 (not_3_out, Opcode[0]);
  not not_4 (not_4_out, Opcode[3]);
  not not_5 (not_5_out, Opcode[3]);
  not not_6 (not_6_out, Opcode[0]);
  not not_7 (not_7_out, Opcode[1]);
  not not_8 (not_8_out, Opcode[2]);
  and and_1 (and_1_out, Opcode[0], not_1_out, Opcode[2], not_2_out);
  and and_2 (and_2_out, not_3_out, Opcode[1], Opcode[2], not_4_out);
  and and_3 (and_3_out, Opcode[0], Opcode[1], Opcode[2], not_5_out);
  and and_4 (and_4_out, not_6_out, not_7_out, not_8_out, Opcode[3]);
  and and_5 (and_5_out, and_1_out, CompVals[0]);
  and and_6 (and_6_out, and_2_out, CompVals[1]);
  and and_7 (and_7_out, and_3_out, CompVals[2]);
  and and_8 (and_8_out, and_4_out, CompVals[3]);
  or or_1 (EnBranch, and_5_out, and_6_out, and_7_out, and_8_out);

  // Notes on the sheet:
  //   the branch control unit
  //   Branch Conditions: bp == 0101
  //   bn == 0110
  //   For conditional branching, each condition is represented
  //   by and individual bit within a 4-bit value that is passed into
  //   bx == 0101 || 0110
  //   bz == 1001 || 1010
  //   ALU comparison results are as close to their corresponding opcodes as possible
  //   bp check
  //   bn check
  //   bx check
  //   bz check
endmodule

module JCONTROL (
  input  [15:0] RS,
  input  [7:0] Output,
  input  [7:0] Immediate,
  input  [3:0] Opcode,
  output JSelect,
  output JALSelect
);

  wire and_1_out, and_2_out, not_1_out, not_2_out, not_3_out, not_4_out;
  wire [7:0] bit_extender_1_out;

  Bit_Extender #(.in_width(16), .out_width(8)) bit_extender_1 (.in(RS), .out(bit_extender_1_out));
  Multiplexer #(.width(8), .enable("false")) multiplexer_1 (
    .in0(bit_extender_1_out), .in1(Immediate), .out(Output), .sel(and_1_out));
  not not_1 (not_1_out, Opcode[1]);
  not not_2 (not_2_out, Opcode[0]);
  not not_3 (not_3_out, Opcode[2]);
  not not_4 (not_4_out, Opcode[1]);
  and and_1 (and_1_out, Opcode[3], not_1_out, Opcode[0]);
  or or_1 (JSelect, and_1_out, and_2_out);
  and and_2 (and_2_out, Opcode[3], Opcode[2], Opcode[1], not_2_out);
  and and_3 (JALSelect, Opcode[3], not_3_out, not_4_out, Opcode[0]);
endmodule
